// Logisim project eee143_lab6_keyboard_template.circ as structural Verilog: 3 circuits, main circuit main
module main (
  output _1_if_write_mode
);

  wire button_1_out, clock_1_out;
  wire [6:0] keyboard_1_data;
  wire [7:0] graphicscontroller_1_display, graphicscontroller_1_display_2, graphicscontroller_1_display_3,
       graphicscontroller_1_display_4;
  wire [63:32] graphicscontroller_1_display_5;

  Clock clock_1 (.out(clock_1_out));
  Button button_1 (.out(button_1_out));
  Keyboard keyboard_1 (.clk(clock_1_out), .data(keyboard_1_data));  // open: re, clr, avail
  // Probe on keyboard_1_data
  graphicsController graphicscontroller_1 (
    .KEY(keyboard_1_data), .CLK(clock_1_out), .RST(button_1_out),
    .Display({graphicscontroller_1_display_5, graphicscontroller_1_display_4, graphicscontroller_1_display_3, graphicscontroller_1_display_2, graphicscontroller_1_display}),
    .WriteMode(_1_if_write_mode));
  DotMatrix #(.matrixcols(8), .matrixrows(8)) dotmatrix_1 (
    .col0(graphicscontroller_1_display_5[63:56]), .col1(graphicscontroller_1_display_5[55:48]),
    .col2(graphicscontroller_1_display_5[47:40]), .col3(graphicscontroller_1_display_5[39:32]),
    .col4(graphicscontroller_1_display_4), .col5(graphicscontroller_1_display_3),
    .col6(graphicscontroller_1_display_2), .col7(graphicscontroller_1_display));
endmodule

module graphicsController (
  input  [6:0] KEY,
  input  CLK,
  input  RST,
  output [63:0] Display,
  output WriteMode
);

  wire [2:0] RX_q, RY_q;
  wire [63:0] cursordecoder_1_cursordisplay, R1_q;

  Register #(.width(64)) R1 (.clk(CLK), .Q(R1_q), .clr(RST));  // open: D, en
  Register #(.width(3)) RX (.clk(CLK), .Q(RX_q), .clr(RST));  // open: D, en
  Register #(.width(3)) RY (.clk(CLK), .Q(RY_q), .clr(RST));  // open: D, en
  cursorDecoder cursordecoder_1 (.X(RX_q), .Y(RY_q), .cursorDisplay(cursordecoder_1_cursordisplay));
  assign Display = R1_q | cursordecoder_1_cursordisplay;  // OR_Gate or_1, 64 bits wide
endmodule

module cursorDecoder (
  input  [2:0] X,
  input  [2:0] Y,
  output [63:0] cursorDisplay
);

  wire [7:0] decoder_1_out0;

  Demultiplexer #(.select(3), .width(8)) demultiplexer_1 (
    .out0(cursorDisplay[63:56]), .out1(cursorDisplay[55:48]), .out2(cursorDisplay[47:40]),
    .out3(cursorDisplay[39:32]), .out4(cursorDisplay[31:24]), .out5(cursorDisplay[23:16]),
    .out6(cursorDisplay[15:8]), .out7(cursorDisplay[7:0]), .in(decoder_1_out0), .sel(X));
  Decoder #(.select(3)) decoder_1 (
    .out0(decoder_1_out0[0]), .out1(decoder_1_out0[1]), .out2(decoder_1_out0[2]), .out3(decoder_1_out0[3]),
    .out4(decoder_1_out0[4]), .out5(decoder_1_out0[5]), .out6(decoder_1_out0[6]), .out7(decoder_1_out0[7]),
    .sel(Y));  // open: en
endmodule
