// Logisim project lab2_143_2s2425_template.circ as structural Verilog: 2 circuits, main circuit main
module main (
);

  wire udlrtranslation_1_down, udlrtranslation_1_left, udlrtranslation_1_right, udlrtranslation_1_up;
  wire [1:0] joystick_1_x, joystick_1_y;

  Joystick #(.bits(2)) joystick_1 (.x(joystick_1_x), .y(joystick_1_y));
  // Probe on joystick_1_x
  // Probe on joystick_1_y
  udlrTranslation udlrtranslation_1 (
    .A(joystick_1_x[1]), .B(joystick_1_x[0]), .C(joystick_1_y[1]), .D(joystick_1_y[0]),
    .Up(udlrtranslation_1_up), .Down(udlrtranslation_1_down), .Left(udlrtranslation_1_left),
    .Right(udlrtranslation_1_right));
  // Probe on udlrtranslation_1_up
  // Probe on udlrtranslation_1_down
  // Probe on udlrtranslation_1_left
  // Probe on udlrtranslation_1_right
endmodule

module udlrTranslation (
  input  A,
  input  B,
  input  C,
  input  D,
  output Up,
  output Down,
  output Left,
  output Right
);


  // Notes on the sheet:
  //   Again, do not move the inputs or the outputs
endmodule
