// Logisim project lab3_143_2s2425_template.circ as structural Verilog: 3 circuits, main circuit main
module main (
  input  [1:0] alu_op,
  input  [3:0] RA,
  input  [3:0] RB,
  output [3:0] RD,
  output [7:0] decoded_top,
  output [7:0] decoded_bot,
  output Z,
  output N,
  output C,
  output O
);

  alu alu_1 (.alu_op(alu_op), .RA(RA), .RB(RB), .RD(RD), .Z(Z), .N(N), .C(C), .O(O));
  double_dec_decoder double_dec_decoder_1 (.RD(RD), .decode_top(decoded_top), .decode_bot(decoded_bot));
  _7_Segment_Display u_7_segment_display_1 (
    .g(decoded_top[7]), .f(decoded_top[6]), .a(decoded_top[5]), .b(decoded_top[4]), .e(decoded_bot[7]),
    .d(decoded_bot[6]), .c(decoded_bot[5]), .dp(decoded_bot[4]));
  _7_Segment_Display u_7_segment_display_2 (
    .g(decoded_top[3]), .f(decoded_top[2]), .a(decoded_top[1]), .b(decoded_top[0]), .e(decoded_bot[3]),
    .d(decoded_bot[2]), .c(decoded_bot[1]), .dp(decoded_bot[0]));
endmodule

module alu (
  input  [1:0] alu_op,
  input  [3:0] RA,
  input  [3:0] RB,
  output [3:0] RD,
  output Z,
  output N,
  output C,
  output O
);
endmodule

module double_dec_decoder (
  input  [3:0] RD,
  output [7:0] decode_top,
  output [7:0] decode_bot
);
endmodule
