// Logisim project lab4_143_2s2425_template.circ as structural Verilog: 4 circuits, main circuit main
module main (
  input  in_1,
  input  in_2,
  input  in_3,
  output out_4,
  output out_5,
  output out_6
);

  wire clock_1_out;

  Clock clock_1 (.out(clock_1_out));
  dffButSR dffbutsr_1 (.D(in_1), .CLK(clock_1_out), .Q(out_4));
  dffButJK dffbutjk_1 (.D(in_2), .CLK(clock_1_out), .Q(out_5));
  dffbutT dffbutt_1 (.D(in_3), .CLK(clock_1_out), .Q(out_6));
endmodule

module dffButJK (
  input  D,
  input  CLK,
  output Q
);

  J_K_Flip_Flop j_k_ff_1 ();  // open: J, K, clk, Q, Qn, preset, reset
endmodule

module dffbutT (
  input  D,
  input  CLK,
  output Q
);

  T_Flip_Flop t_ff_1 ();  // open: T, clk, Q, Qn, reset, preset
endmodule

module dffButSR (
  input  D,
  input  CLK,
  output Q
);

  S_R_Flip_Flop s_r_ff_1 ();  // open: S, R, clk, Q, reset, Qn, preset
endmodule
