// Logisim project lab5_143_2s2425_template.circ as structural Verilog: 2 circuits, main circuit main
module main (
  output [2:0] yValOut,
  output [2:0] xValOut
);

  wire button_1_out, clock_1_out;
  wire [1:0] joystick_1_x, joystick_1_y;
  wire [7:0] decoder_1_out0, demultiplexer_1_out0, demultiplexer_1_out1, demultiplexer_1_out2,
       demultiplexer_1_out3, demultiplexer_1_out4, demultiplexer_1_out5, demultiplexer_1_out6,
       demultiplexer_1_out7;

  Clock clock_1 (.out(clock_1_out));
  Button button_1 (.out(button_1_out));
  Joystick #(.bits(2)) joystick_1 (.x(joystick_1_x), .y(joystick_1_y));
  DotMatrix #(.matrixcols(8), .matrixrows(8)) dotmatrix_1 (
    .col0(demultiplexer_1_out0), .col1(demultiplexer_1_out1), .col2(demultiplexer_1_out2),
    .col3(demultiplexer_1_out3), .col4(demultiplexer_1_out4), .col5(demultiplexer_1_out5),
    .col6(demultiplexer_1_out6), .col7(demultiplexer_1_out7));
  xyTracker xytracker_1 (
    .stickY(joystick_1_y), .stickX(joystick_1_x), .CLK(clock_1_out), .RST(button_1_out), .pixelY(yValOut),
    .pixelX(xValOut));
  Demultiplexer #(.select(3), .width(8)) demultiplexer_1 (
    .out0(demultiplexer_1_out0), .out1(demultiplexer_1_out1), .out2(demultiplexer_1_out2),
    .out3(demultiplexer_1_out3), .out4(demultiplexer_1_out4), .out5(demultiplexer_1_out5),
    .out6(demultiplexer_1_out6), .out7(demultiplexer_1_out7), .in(decoder_1_out0), .sel(xValOut));
  Decoder #(.select(3)) decoder_1 (
    .out0(decoder_1_out0[0]), .out1(decoder_1_out0[1]), .out2(decoder_1_out0[2]), .out3(decoder_1_out0[3]),
    .out4(decoder_1_out0[4]), .out5(decoder_1_out0[5]), .out6(decoder_1_out0[6]), .out7(decoder_1_out0[7]),
    .sel(yValOut));  // open: en
endmodule

module xyTracker (
  input  [1:0] stickY,
  input  [1:0] stickX,
  input  CLK,
  input  RST,
  output [2:0] pixelY,
  output [2:0] pixelX
);
endmodule
